# Fritzing sketch DFPlayer (saved by Fritzing 0.9.3b)

parts:
  Q1 = PNP-Transistor [package="TO92 [THT]"]
  WeMos_D1_Mini1 = WeMos D1 Mini
  R1 = Resistor [tolerance=±5% resistance=10k package="0402 [SMD]"]
  R2 = Resistor [tolerance=±5% resistance=4.7k package="0402 [SMD]"]
  U1 = RELAY [package=OJ]
  D1 = Rectifier Diode [part_number=1N4001 package="300 mil [THT]"]
  SPKR1 = Loudspeaker
  DFRobot_DFPlayer_Mini1 = DFRobot DFPlayer Mini [part_number=DFR0299]
  R3 = Resistor [tolerance=±5% resistance=1k package="0402 [SMD]"]

nets:
  5V: Q1.E, WeMos_D1_Mini1.5V, R2.Pin_1, DFRobot_DFPlayer_Mini1.VCC
  N1: Q1.B, R1.Pin_1, R2.Pin_0
  N2: Q1.C, U1.COIL2, D1.cathode
  N3: WeMos_D1_Mini1.D1, R3.Pin_0
  N4: WeMos_D1_Mini1.D2, DFRobot_DFPlayer_Mini1.TX
  N5: WeMos_D1_Mini1.D5, DFRobot_DFPlayer_Mini1.BUSY
  N6: WeMos_D1_Mini1.D6, R1.Pin_0
  N7: WeMos_D1_Mini1.G, U1.COIL1, D1.anode, DFRobot_DFPlayer_Mini1.GND-1, DFRobot_DFPlayer_Mini1.GND-2
  N8: U1.MAIN, DFRobot_DFPlayer_Mini1.SPK_1
  N9: U1.NO, SPKR1.pin2
  N10: SPKR1.pin1, DFRobot_DFPlayer_Mini1.SPK_2
  N11: DFRobot_DFPlayer_Mini1.RX, R3.Pin_1
